# Fritzing sketch transceiver_gloveV2 (saved by Fritzing 0.9.3b)
breadboards: 1

parts:
  Composant1 = Arduino Nano (Rev3.0)
  R2 = Resistor [tolerance=±5% resistance=62k package=THT]
  R1 = Basic Flex Resistor
  Composant2 = NRF24L01+ Breakout Board
  R3 = Basic Flex Resistor
  R4 = Basic Flex Resistor
  R5 = Resistor [tolerance=±5% resistance=4.7k package=THT]
  R6 = Resistor [tolerance=±5% resistance=4.7k package=THT]
  VCC1 = Battery block 9V

nets:
  GND: Composant1.GND, R2.Pin_0, Composant2.GND, R5.Pin_0, R6.Pin_0, VCC1.-
  N1: Composant1.D7, Composant2.CE
  N2: Composant1.D8, Composant2.CS
  N3: Composant1.D11/MOSI, Composant2.MOSI
  N4: Composant1.D12/MISO, Composant2.MISO
  N5: Composant1.VIN, VCC1.+
  5V: Composant1.5V, R1.Pin_2, Composant2.VCC, R3.Pin_2, R4.Pin_2
  N6: Composant1.A2, R2.Pin_1, R1.pin_1
  N7: Composant1.A1, R3.pin_1, R6.Pin_1
  N8: Composant1.A0, R4.pin_1, R5.Pin_1
  N9: Composant1.D13/SCK, Composant2.SCK
