# Fritzing sketch transceiver_glove (saved by Fritzing 0.9.3b)
breadboards: 1

parts:
  Composant1 = Arduino Nano (Rev3.0)
  R2 = Resistor [tolerance=±5% resistance=62k package=THT]
  R1 = Basic Flex Resistor
  Composant2 = NRF24L01+ Breakout Board
  VCC1 = Battery block 9V

nets:
  GND: Composant1.GND, R2.Pin_0, Composant2.GND, VCC1.-
  N1: Composant1.D7, Composant2.CE
  N2: Composant1.D8, Composant2.CS
  N3: Composant1.D11/MOSI, Composant2.MOSI
  N4: Composant1.D12/MISO, Composant2.MISO
  N5: Composant1.VIN, VCC1.+
  5V: Composant1.5V, R1.Pin_2, Composant2.VCC
  N6: Composant1.A0, R2.Pin_1, R1.pin_1
  N7: Composant1.D13/SCK, Composant2.SCK
